// Logisim project lab2.circ as structural Verilog: 1 circuit, main circuit main
module main (
  input  S1,
  input  S0,
  input  A1,
  input  A0,
  input  B1,
  input  B0,
  output X2,
  output X1,
  output X0,
  output Y7,
  output Y6,
  output Y5,
  output Y4,
  output Y3,
  output Y2,
  output Y1,
  output Y0
);

  wire and_1_out, and_2_out, and_3_out, and_4_out, and_5_out, n3_to_8_decoder_74138_1_p7,
       n3_to_8_decoder_74138_1_p8, n3_to_8_decoder_74138_1_p9, n3_to_8_decoder_74138_1_p10,
       n3_to_8_decoder_74138_1_p11, n3_to_8_decoder_74138_1_p12, n3_to_8_decoder_74138_1_p13,
       n3_to_8_decoder_74138_1_p14, not_1_out, not_2_out, not_3_out, not_4_out, not_5_out, not_6_out,
       not_7_out, not_8_out, not_9_out, not_10_out, or_1_out, or_2_out, or_3_out, or_4_out, or_5_out,
       xor_1_out, xor_2_out, xor_3_out;

  not not_1 (not_1_out, A0);
  not not_2 (not_2_out, B1);
  not not_3 (not_3_out, A1);
  and and_1 (and_1_out, not_1_out, B0);
  or or_1 (or_1_out, A1, not_2_out);
  or or_2 (or_2_out, not_3_out, B1);
  or or_3 (or_3_out, A1, B1);
  and and_2 (and_2_out, not_3_out, B1);
  xor xor_1 (xor_1_out, A1, B1);
  and and_3 (and_3_out, and_1_out, or_2_out);
  and and_4 (and_4_out, A0, or_1_out);
  and and_5 (and_5_out, or_2_out, B0);
  xor xor_2 (xor_2_out, and_1_out, xor_1_out);
  or or_4 (or_4_out, and_3_out, and_2_out);
  or or_5 (or_5_out, and_4_out, and_5_out);
  not not_4 (not_4_out, 1'b1);
  xor xor_3 (xor_3_out, A0, B0);
  not not_5 (not_5_out, 1'b1);
  not not_6 (not_6_out, 1'b1);
  not not_7 (not_7_out, 1'b1);
  // _4_to_1_MUX__x2___74153 #(.Facing("east")) 4_to_1_mux_x2_74153_1: pin names not known; wires that end beside it: or_4_out, not_7_out, A1, B1, xor_2_out, or_3_out, not_7_out, not_7_out, X2, X1
  // _4_to_1_MUX__x2___74153 #(.Facing("east")) 4_to_1_mux_x2_74153_2: pin names not known; wires that end beside it: A0, B0, xor_3_out, or_5_out, 1'b1, not_5_out, S0, not_4_out, S0, S1, not_4_out, S1, X0
  not not_8 (not_8_out, X1);
  not not_9 (not_9_out, X2);
  not not_10 (not_10_out, X0);
  // _3_to_8_decoder__74138 #(.Facing("east")) 3_to_8_decoder_74138_1: pin names not known; wires that end beside it: not_10_out, not_8_out, not_9_out, 1'b1, not_6_out, not_6_out, n3_to_8_decoder_74138_1_p7, n3_to_8_decoder_74138_1_p8, n3_to_8_decoder_74138_1_p9, n3_to_8_decoder_74138_1_p10, n3_to_8_decoder_74138_1_p11, n3_to_8_decoder_74138_1_p12, n3_to_8_decoder_74138_1_p13, n3_to_8_decoder_74138_1_p14
  not not_11 (Y7, n3_to_8_decoder_74138_1_p7);
  not not_12 (Y1, n3_to_8_decoder_74138_1_p13);
  not not_13 (Y0, n3_to_8_decoder_74138_1_p14);
  not not_14 (Y6, n3_to_8_decoder_74138_1_p8);
  not not_15 (Y5, n3_to_8_decoder_74138_1_p9);
  not not_16 (Y4, n3_to_8_decoder_74138_1_p10);
  not not_17 (Y3, n3_to_8_decoder_74138_1_p11);
  not not_18 (Y2, n3_to_8_decoder_74138_1_p12);
endmodule
